# Fritzing sketch Traktorinoa (saved by Fritzing 0.9.1b)
breadboards: 1

parts:
  IC1 = L293D [package=THT]
  BAT1 = BC9VPC [package=bc9vpc]
  M1 = DC Motor
  M2 = DC Motor
  Sonar = SRF05 Ultrasonic Rangefinder
  Parte1 = Arduino Uno (Rev3)
  J1 = Basic Servo

nets:
  N1: IC1.Enable_1, IC1.+Vmotor, BAT1.V-
  N2: IC1.In_1, Parte1.D2
  N3: IC1.Out_1_(_Controlled_by_Enable_1_), M2.pin_2
  GND: IC1.0V, BAT1.V+, Sonar.GND, J1.gnd
  N4: IC1.Out_2_(_Controlled_by_Enable_1_), M2.pin_1
  N5: IC1.In_2, Parte1.D3_PWM
  VCC: IC1.Enable_2, IC1.+V, Sonar.VCC, J1.vcc
  N6: IC1.In_3, Parte1.D7
  N7: IC1.Out_3_(_Controlled_by_Enable_2_), M1.pin_2
  N8: IC1.Out_4_(_Controlled_by_Enable_2_), M1.pin_1
  N9: IC1.In_4, Parte1.D8
  N10: Sonar.Trig, Parte1.D10_PWM/SS
  N11: Sonar.Echo, Parte1.D11_PWM/MOSI
  N12: Parte1.D5_PWM, J1.pulse
